# Fritzing sketch factory_sketch (saved by Fritzing 0.9.5d)
breadboards: 1

parts:
  A1 = Raspberry Pi 5
  IC1 = ULN2003A [package="DIP16 [THT]"]

nets:
  N1: A1.GPIO17, IC1.In_1
  N2: A1.GPIO27, IC1.In_2
  N3: A1.GPIO22, IC1.In_3
  N4: A1.GPIO23, IC1.In_4

custom parts:
  Raspberry Pi 5: The RPi5, a faster version of the awesome Raspberry Pi4B ARM Board with 40 pin gpio.
